# Fritzing sketch TTP229 (saved by Fritzing 0.9.3b)

parts:
  ZS-042_RTC1 = ZS-042 RTC Module
  元件1 = Arduino Uno (Rev3)

nets:
  GND: ZS-042_RTC1.GND, 元件1.GND
  N1: ZS-042_RTC1.SCL, 元件1.D2
  N2: ZS-042_RTC1.SDO, 元件1.D3_PWM

custom parts:
  ZS-042 RTC Module: This is the ZS-042 RTC module which uses the Maxim DS3231 real time clock IC. The module has a battery holder for a LIR2032 or CR2032. The module also includes an Atmel AT24C32 32K EEPROM for storing important information. The module can operate at 3V3 and 5V.
